# Fritzing sketch Prefboard2 (saved by Fritzing 0.9.2b)
perfboards: 2

parts:
  IC1 = MICROCONTROLLER [package=dil28-3]
  XTAL1 = Crystal [frequency="16 Mhz" package=THT]
  Q2 = PNP-Transistor [package="SOT-23 [SMD]"]  # not connected
  R2 = Resistor [tolerance=±5% resistance=220 package=THT]
  R3 = Resistor [tolerance=±5% resistance=220 package=THT]
  IC2 = Voltage Regulator [package=to220-igo]
  LED1 = LED - 3mm [color="Red (633nm)" package="3 mm [THT]"]  # not connected
  S2 = Pushbutton [package="[SMD]"]
  S3 = Pushbutton [package="[SMD]"]
  J1 = male pin header, 1 pin [form="♂ (male)"]
  J2 = male pin header, 1 pin [form="♂ (male)"]  # not connected
  J3 = male pin header, 1 pin [form="♂ (male)"]  # not connected
  Y1 = Resonator [frequency="16 Mhz" package=THT]  # not connected
  C1 = Electrolytic Capacitor [capacitance=1μF package="0405 [SMD, electrolytic]"]  # not connected
  C2 = Capacitor [package=cap-pth-small]  # not connected
  C3 = Ceramic Capacitor [capacitance="100 nF" voltage=50V package="0603 [SMD, multilayer]"]  # not connected
  J4 = male pin header, 1 pin [form="♂ (male)"]
  R1 = Resistor [tolerance=±5% resistance=220 package=THT]
  IC4 = Voltage Regulator [package=to220-igo]  # not connected

nets:
  N1: IC1.PC6(_RESET), S2.Pin_1, S2.Pin_2, R1.Pin_1
  N2: IC1.PD2(INT0), R3.Pin_1
  N3: IC1.PD3(INT1), R2.Pin_1
  N4: IC1.VCC, IC1.AGND
  N5: IC1.PB6(XTAL1_TOSC1), XTAL1.pin_1
  N6: IC1.PD6(AIN0), J1.pin1, J4.pin1
  N7: IC1.PD7(AIN1), S3.Pin_1, S3.Pin_2
  N8: IC1.AVCC, IC2.OUT
  N9: S2.Pin_3, S2.Pin_4
  N10: S3.Pin_3, S3.Pin_4
